# Fritzing sketch Quad_AK (saved by Fritzing 0.9.2b)
circuit board: 8.46667cm x 5.64444cm

parts:
  MPU6050 = MPU-6050 Board GY-521 [form="♀ (female)" package=THT]
  LiPo_3S = LC-R121R3P
  L7805CV = Voltage Regulator [package=to-220-alt]
  C1_104 = Capacitor [package=cap-pth-small-kit]
  U1 = atmega328 [package=dip]
  ESC_1 = Basic Servo
  ESC_2 = Basic Servo
  ESC_3 = Basic Servo
  ESC_4 = Basic Servo
  J6 = female pin header, 2 pins [form="♀ (female)"]
  J5 = rounded female pin header, 12 pins [form="♀ (female rounded)"]
  LED1 = LED - 5mm [color="Green (570nm)" package="5 mm [THT]"]
  R1 = Resistor [tolerance=±5% resistance=330 package=THT]
  J7 = male pin header, 2 pins [form="♂ (male)"]
  J8 = male pin header, 2 pins [form="♂ (male)"]

nets:
  N1: MPU6050.pin1, L7805CV.OUT, C1_104.2, U1.VCC, U1.AREF, J6.pin1, J5.pin2, J5.pin5, J5.pin8, J5.pin11, J7.pin1
  GND: MPU6050.pin2, LiPo_3S.pin2, L7805CV.GND, C1_104.1, U1.GND, ESC_1.gnd, ESC_2.gnd, ESC_3.gnd, ESC_4.gnd, J6.pin2, J5.pin3, J5.pin6, J5.pin9, J5.pin12, R1.Pin_1, J8.pin2
  N2: MPU6050.pin3, U1.A5
  N3: MPU6050.pin4, U1.A4
  N4: LiPo_3S.pin1, L7805CV.IN
  N5: U1.D0_(RX), J8.pin1
  N6: U1.D1_(TX), J7.pin2
  N7: U1.D4, ESC_4.pulse
  N8: U1.D5_(PWM), ESC_3.pulse
  N9: U1.D6_(PWM), ESC_2.pulse
  N10: U1.D7, ESC_1.pulse
  N11: U1.D8, J5.pin10
  N12: U1.D9_(PWM), J5.pin7
  N13: U1.D10_(PWM), J5.pin4
  N14: U1.D11_(PWM), J5.pin1
  N15: U1.D12, LED1.anode
  VCC: ESC_1.vcc, ESC_2.vcc, ESC_3.vcc, ESC_4.vcc
  N16: LED1.cathode, R1.Pin_0

notes:
  Receiver
  Sig
  GND
  +5v
  Vcc
  SDL
  SCL
  MPU6050
  L7805CV
  LiPo 3S
  RX
  +5v / NC
  TX
  AK ATmega328P Quadcopter, First design of the quadcopter flight controller., 1.0

custom parts:
  MPU-6050 Board GY-521: Acelerometro y Giroscopio MPU-6050 Board GY-521
  LC-R121R3P: 12V 1.Ah battery
